// Logisim project S1-T4.circ as structural Verilog: 1 circuit, main circuit main
module main (
  output [6:0] out_1
);

  wire comparator_1_eq, comparator_2_eq, comparator_3_eq, comparator_4_eq, comparator_5_eq, comparator_6_eq,
       comparator_7_eq, comparator_7_gt, Dice_Number_out, or_1_out, or_2_out, or_3_out, Reset_out;
  wire [2:0] adder_1_out, DICE_out, divider_1_out;
  wire [6:0] adder_2_out, bit_extender_1_out, multiplexer_1_out, multiplexer_7_out;

  Random #(.width(3)) DICE (.clk(Dice_Number_out), .out(DICE_out), .clr(Reset_out));  // open: next
  Button Dice_Number (.out(Dice_Number_out));
  Divider #(.width(3)) divider_1 (.a(DICE_out), .b(3'b110), .out(divider_1_out));  // open: upper, rem
  Button Reset (.out(Reset_out));
  Adder #(.width(3)) adder_1 (.a(divider_1_out), .b(3'b001), .out(adder_1_out));  // open: cin, cout
  Register #(.width(7)) Player_Position (
    .D(multiplexer_7_out), .Q(out_1), .clk(Dice_Number_out), .clr(comparator_7_gt));  // open: en
  Comparator #(.width(7), .mode("unsigned")) comparator_1 (
    .a(out_1), .b(7'b0010001), .eq(comparator_1_eq));  // open: gt, lt
  Comparator #(.width(7), .mode("unsigned")) comparator_2 (
    .a(out_1), .b(7'b0111110), .eq(comparator_2_eq));  // open: gt, lt
  Comparator #(.width(7), .mode("unsigned")) comparator_3 (
    .a(out_1), .b(7'b1010111), .eq(comparator_3_eq));  // open: gt, lt
  assign bit_extender_1_out = {{4{1'b0}}, adder_1_out};  // Bit_Extender bit_extender_1
  Multiplexer #(.width(7), .enable("false")) multiplexer_1 (
    .in1(7'b0000111), .out(multiplexer_1_out), .sel(comparator_1_eq));  // open: in0
  Multiplexer #(.width(7), .enable("false")) multiplexer_2 (
    .in1(7'b0010011), .out(multiplexer_1_out), .sel(comparator_2_eq));  // open: in0
  Multiplexer #(.width(7), .enable("false")) multiplexer_3 (
    .in1(7'b0100100), .out(multiplexer_1_out), .sel(comparator_3_eq));  // open: in0
  or or_1 (or_1_out, comparator_1_eq, comparator_2_eq, comparator_3_eq);
  Adder #(.width(7)) adder_2 (.a(bit_extender_1_out), .b(out_1), .out(adder_2_out));  // open: cin, cout
  LED led_1 (.in(or_1_out));
  Comparator #(.width(7), .mode("unsigned")) comparator_4 (
    .a(out_1), .b(7'b0001001), .eq(comparator_4_eq));  // open: gt, lt
  Comparator #(.width(7), .mode("unsigned")) comparator_5 (
    .a(out_1), .b(7'b0011100), .eq(comparator_5_eq));  // open: gt, lt
  Comparator #(.width(7), .mode("unsigned")) comparator_6 (
    .a(out_1), .b(7'b0111111), .eq(comparator_6_eq));  // open: gt, lt
  Comparator #(.width(7), .mode("unsigned")) comparator_7 (
    .a(adder_2_out), .b(7'b1100100), .gt(comparator_7_gt), .eq(comparator_7_eq));  // open: lt
  Multiplexer #(.width(7), .enable("false")) multiplexer_4 (
    .in1(7'b0011111), .out(multiplexer_1_out), .sel(comparator_4_eq));  // open: in0
  Multiplexer #(.width(7), .enable("false")) multiplexer_5 (
    .in1(7'b1010100), .out(multiplexer_1_out), .sel(comparator_5_eq));  // open: in0
  Multiplexer #(.width(7), .enable("false")) multiplexer_6 (
    .in1(7'b1010001), .out(multiplexer_1_out), .sel(comparator_6_eq));  // open: in0
  LED led_2 (.in(comparator_7_eq));
  LED led_3 (.in(or_2_out));
  or or_2 (or_2_out, comparator_6_eq, comparator_5_eq, comparator_4_eq);
  Multiplexer #(.width(7), .enable("false")) multiplexer_7 (
    .in0(adder_2_out), .in1(multiplexer_1_out), .out(multiplexer_7_out), .sel(or_3_out));
  or or_3 (or_3_out, comparator_4_eq, comparator_5_eq, comparator_6_eq, comparator_1_eq, comparator_2_eq, comparator_3_eq);

  // Notes on the sheet:
  //   Position Indicator
  //   Modulo Operator
  //   To make input 1-6
  //   Snake 17->7
  //   Snake 62-->19
  //   Snake 87->36
  //    convert to7-bit input
  //   Adding to original Position
  //   Snake Light
  //   Ladder 9->31
  //   Ladder 28->84
  //   Ladder 63->81
  //   Circuit Design for Snakes and Ladders Game
  //   Ladder Light
  //   1. Tap the button of the dice to randomly generate the number
  //   3. The Reset button is used to reset the dice 
  //   5. The LED glows as the player reaches 100
  //   Instructions :
  //   2. The counter of Player position reset to 0 as soon as the position reaches to 64
  //   4. The Position is updated according to the tail of snakes and tip of ladders
  //   6. Yellow Light glows when snake encounters and blue for Ladder
endmodule
